// Logisim project AND_BLOCK.circ as structural Verilog: 1 circuit, main circuit main
module main (
  input  A3,
  input  A2,
  input  A1,
  input  A0,
  input  B3,
  input  B2,
  input  B1,
  input  B0,
  output O3,
  output O2,
  output O1,
  output O0
);

  and and_1 (O3, A3, B3);
  and and_2 (O2, A2, B2);
  and and_3 (O1, A1, B1);
  and and_4 (O0, A0, B0);
endmodule
