// Logisim project Full adder.circ as structural Verilog: 1 circuit, main circuit Full adder
module Full_adder (
  input  in_1,
  input  in_2,
  input  in_3,
  output out_4,
  output out_5
);

  wire half_adder_1_p3, half_adder_1_p4, half_adder_2_p4;

  // Half_adder half_adder_1: pin names not known; wires that end beside it: in_1, in_2, half_adder_1_p3, half_adder_1_p4
  // Half_adder half_adder_2: pin names not known; wires that end beside it: half_adder_1_p3, in_3, out_4, half_adder_2_p4
  or or_1 (out_5, half_adder_2_p4, half_adder_1_p4);
endmodule
