// Logisim project OR_BLOCK.circ as structural Verilog: 1 circuit, main circuit main
module main (
  input  A3,
  input  A2,
  input  A1,
  input  A0,
  input  B3,
  input  B2,
  input  B1,
  input  B0,
  output O3,
  output O2,
  output O1,
  output O0
);

  or or_1 (O3, A3, B3);
  or or_2 (O2, A2, B2);
  or or_3 (O1, A1, B1);
  or or_4 (O0, A0, B0);
endmodule
